# Fritzing sketch arduinorfidservo (saved by Fritzing 0.9.3b)
breadboards: 1

parts:
  J1 = Piezo Speaker
  Part2 = Arduino Nano (Rev3.0)
  J2 = Basic Servo
  Part3 = RFID-RC522-v2
  LED4 = RGB LED (com. cathode, rgb) [package="5 mm [THT]"]
  R1 = Resistor [tolerance=±5% resistance=330 package=THT]
  R2 = Resistor [tolerance=±5% resistance=330 package=THT]
  R3 = Resistor [tolerance=±5% resistance=330 package=THT]

nets:
  GND: J1.pin1, Part2.GND, J2.gnd, Part3.GND, LED4.common_cathode
  N1: J1.pin2, Part2.D2
  N2: Part2.D3, J2.pulse
  N3: Part2.D6, R3.Pin_1
  N4: Part2.D7, R1.Pin_1
  N5: Part2.D8, R2.Pin_1
  N6: Part2.D9, Part3.RST
  N7: Part2.D10, Part3.SDA
  N8: Part2.D11/MOSI, Part3.MOSI
  N9: Part2.D12/MISO, Part3.MISO
  5V: Part2.5V, J2.vcc
  3V3: Part2.3V3, Part3.3.3V
  N10: Part2.D13/SCK, Part3.SCK
  N11: LED4.red_anode, R3.Pin_0
  N12: LED4.green_anode, R1.Pin_0
  N13: LED4.blue_anode, R2.Pin_0

custom parts:
  RFID-RC522-v2: A simple China made RFID-RC522 Reader; do check the pin labels, as this is a MFRC522 based clone.
